# Fritzing sketch Accelerometer (saved by Fritzing 0.8.7b)
circuit board: 13.2009cm x 7.95218cm
perfboards: 1

parts:
  Microcontroller = Arduino Mega 2560 (Rev3)
  Accelerometer = Triple Axis Accelerometer Breakout - ADXL335

nets:
  N1: Microcontroller.A0, Accelerometer.XOUT
  N2: Microcontroller.A1, Accelerometer.YOUT
  N3: Microcontroller.A2, Accelerometer.ZOUT
  N4: Microcontroller.D21/SCL, Microcontroller.SCL, Accelerometer.ST
  3V3: Microcontroller.3V3, Accelerometer.VCC
  GND: Microcontroller.GND, Accelerometer.GND
